# Fritzing sketch oasis (saved by Fritzing 0.9.3b)
circuit board: 8.46667cm x 5.64444cm
breadboards: 1

parts:
  WeMos_D1_Mini2 = WeMos D1 Mini
  U1 = 74HC4052 [package=dil16]
  J1 = JST-03JQ-BT [part_number=JST-JQ-BT package=THT]
  J3 = JST-03JQ-BT [part_number=JST-JQ-BT package=THT]
  J4 = JST-03JQ-BT [part_number=JST-JQ-BT package=THT]
  J6 = JST-03JQ-BT [part_number=JST-JQ-BT package=THT]
  J7 = JST-03JQ-BT [part_number=JST-JQ-BT package=THT]
  J8 = JST-03JQ-BT [part_number=JST-JQ-BT package=THT]
  J9 = JST-03JQ-BT [part_number=JST-JQ-BT package=THT]
  J10 = JST-03JQ-BT [part_number=JST-JQ-BT package=THT]
  K1 = Relay [part_number=FRS1B-S package=THT]  # not connected

nets:
  N1: WeMos_D1_Mini2.A0, U1.Y
  N2: WeMos_D1_Mini2.D5, U1.B
  N3: WeMos_D1_Mini2.D6, U1.A
  N4: WeMos_D1_Mini2.D7, U1.X3
  N5: U1.Y1, J7.pin1
  N6: U1.INH, U1.VEE, U1.GND
  N7: J1.pin2, J3.pin2, J6.pin2, J7.pin2
  N8: J1.pin3, J6.pin3, J7.pin3
  N9: J4.pin2, J8.pin2, J9.pin2, J10.pin2
  N10: J4.pin3, J8.pin3, J9.pin3, J10.pin3
